# Fritzing sketch OpenFluxl Circuit v.0.1 (saved by Fritzing 0.9.1b)
breadboards: 1

parts:
  MD1 = mystery part, 8 pins [part_number=MIC4422 chip_label=?]
  C1 = Ceramic Capacitor [capacitance=0.1mF part_number=EEUFR1C101 package="100 mil [THT, multilayer]"]
  Microcontroller = Arduino Uno (Rev3) - ICSP
  R1 = Resistor [tolerance=±5% resistance=10k part_number=CFR16J10K package=THT]
  Q1 = Basic FET N-Channel [part_number=IRFP260N package="TO220 [THT]"]
  L1 = Inductor [part_number=ELC09D102F current=280mA inductance=1mH package="400 mil [THT]"]
  C2 = Ceramic Capacitor [capacitance=1mF part_number=ECA1CAM102X package="100 mil [THT, multilayer]"]
  C3 = Ceramic Capacitor [capacitance=0.1mF part_number=EEUEE2E10 package="100 mil [THT, multilayer]"]
  JP1 = Header 2 [package=screwterminal-3.5mm-2_lock]
  R2 = Resistor [tolerance=±5% resistance=10M part_number=CFR25J10M package=THT]
  R3 = Resistor [tolerance=±5% resistance=100k part_number=LR1F100K package=THT]
  R4 = Resistor [tolerance=±5% resistance=100k part_number=LR1F100K package=THT]
  C4 = Ceramic Capacitor [capacitance=10pF part_number=C315C100J2G5TA package="100 mil [THT, multilayer]"]
  D1 = Schottky Diode [part_number=MBR40250TG package="300 mil [THT]"]
  Q2 = Basic FET N-Channel [part_number=SIHF15N60E-E3 package="TO220 [THT]"]
  R5 = Resistor [tolerance=±5% resistance=220 part_number=MCMF006FF2200A50 package=THT]
  LED1 = LED - 5mm [color="Red (633nm)" part_number=703-0100 package="5 mm [THT]"]
  R6 = Resistor [tolerance=±5% resistance=10k part_number=LR1F100K package=THT]
  PAD0 = mystery part, 1 pin [chip_label=?]
  S1 = Pushbutton [part_number=MC34224-071-1601 package=THT]
  Q3 = Basic FET N-Channel [part_number=SIHF15N60E-E3 package="TO220 [THT]"]
  R7 = Resistor [tolerance=±5% resistance=220 part_number=MCMF006FF2200A50 package=THT]
  LED2 = LED - 5mm [color="Red (633nm)" part_number=703-0100 package="5 mm [THT]"]
  R8 = Resistor [tolerance=±5% resistance=10k part_number=LR1F100K package=THT]
  PAD1 = mystery part, 1 pin [chip_label=?]
  Q4 = Basic FET N-Channel [part_number=SIHF15N60E-E3 package="TO220 [THT]"]
  R9 = Resistor [tolerance=±5% resistance=220 part_number=MCMF006FF2200A50 package=THT]
  LED3 = LED - 5mm [color="Red (633nm)" part_number=703-0100 package="5 mm [THT]"]
  R10 = Resistor [tolerance=±5% resistance=10k part_number=LR1F100K package=THT]
  PAD2 = mystery part, 1 pin [chip_label=?]
  Q5 = Basic FET N-Channel [part_number=SIHF15N60E-E3 package="TO220 [THT]"]
  R11 = Resistor [tolerance=±5% resistance=220 part_number=MCMF006FF2200A50 package=THT]
  LED4 = LED - 5mm [color="Red (633nm)" part_number=703-0100 package="5 mm [THT]"]
  R12 = Resistor [tolerance=±5% resistance=10k part_number=LR1F100K package=THT]
  PAD3 = mystery part, 1 pin [chip_label=?]
  Q6 = Basic FET N-Channel [part_number=SIHF15N60E-E3 package="TO220 [THT]"]
  R13 = Resistor [tolerance=±5% resistance=220 part_number=MCMF006FF2200A50 package=THT]
  R14 = Resistor [tolerance=±5% resistance=10k part_number=LR1F100K package=THT]
  PAD4 = mystery part, 1 pin [chip_label=?]
  Q7 = Basic FET N-Channel [part_number=SIHF15N60E-E3 package="TO220 [THT]"]
  R15 = Resistor [tolerance=±5% resistance=220 part_number=MCMF006FF2200A50 package=THT]
  LED6 = LED - 5mm [color="Red (633nm)" part_number=703-0100 package="5 mm [THT]"]
  R16 = Resistor [tolerance=±5% resistance=10k part_number=LR1F100K package=THT]
  PAD5 = mystery part, 1 pin [chip_label=?]
  LED5 = LED - 5mm [color="Red (633nm)" part_number=703-0100 package="5 mm [THT]"]
  D2 = Zener Diode [part_number=P6KE350A breakdown_voltage=3.6V package="300 mil [THT]"]

nets:
  12V: MD1.pin1, MD1.pin8, C1.1, Microcontroller.VIN, L1.pin_0, C2.1
  N1: MD1.pin2, Microcontroller.D3_PWM, R1.Pin_1
  GND: MD1.pin4, MD1.pin5, C1.0, Microcontroller.GND, R1.Pin_0, Q1.source, C2.0, C3.0, JP1.2, R4.Pin_0, C4.0, Q2.source, LED1.cathode, Q3.source, LED2.cathode, Q4.source, LED3.cathode, Q5.source, LED4.cathode, Q6.source, Q7.source, LED6.cathode, LED5.cathode, D2.anode
  N2: MD1.pin6, MD1.pin7, Q1.gate
  N3: Microcontroller.A0, R2.Pin_0, R3.Pin_1, C4.1
  N4: Microcontroller.ICSP_MISO, Microcontroller.D12/MISO, Q7.gate, R15.Pin_1
  N5: Microcontroller.ICSP_MOSI, Microcontroller.D11_PWM/MOSI, Q6.gate, R13.Pin_1
  N6: Microcontroller.D8, Q3.gate, R7.Pin_1
  N7: Microcontroller.D9_PWM, Q4.gate, R9.Pin_1
  N8: Microcontroller.D10_PWM/SS, Q5.gate, R11.Pin_1
  N9: Microcontroller.D7, Q2.gate, R5.Pin_1
  N10: Q1.drain, L1.pin_1, D1.anode
  N11: C3.1, JP1.1, R2.Pin_1, D1.cathode, S1.leg0, D2.cathode
  N12: R3.Pin_0, R4.Pin_1
  N13: Q2.drain, R6.Pin_0, PAD0.pin1
  N14: R5.Pin_0, LED1.anode
  N15: R6.Pin_1, S1.leg1, R8.Pin_1, R10.Pin_1, R12.Pin_1, R14.Pin_1, R16.Pin_1
  N16: Q3.drain, R8.Pin_0, PAD1.pin1
  N17: R7.Pin_0, LED2.anode
  N18: Q4.drain, R10.Pin_0, PAD2.pin1
  N19: R9.Pin_0, LED3.anode
  N20: Q5.drain, R12.Pin_0, PAD3.pin1
  N21: R11.Pin_0, LED4.anode
  N22: Q6.drain, R14.Pin_0, PAD4.pin1
  N23: R13.Pin_0, LED5.anode
  N24: Q7.drain, R16.Pin_0, PAD5.pin1
  N25: R15.Pin_0, LED6.anode

notes:
  HV
  GND
